# Fritzing sketch practice13 (saved by Fritzing 0.9.5d)
breadboards: 1

parts:
  U1 = LuaNode32 / ESP32 [part_number=ESP32S-PIN30]
  R1 = Resistor [tolerance=±5% resistance=1k package=THT]
  R4 = Resistor [tolerance=±5% resistance=2.2k package=THT]
  パーツ1 = Voltage Sensor 25V

nets:
  N1: U1.D32, R1.Pin_1, R4.Pin_0
  N2: U1.GND, R4.Pin_1
  N3: U1.Vin, パーツ1.+, パーツ1.-
  N4: R1.Pin_0, パーツ1.S

notes:
  1kΩ
  2kΩ

custom parts:
  LuaNode32 / ESP32: New Image for LuaNode32 DOIT ESP32 DEVKIT V1. Base parts from LuaNode32 / ESP32 ESP32 based LuaNode32 by G.Noorlander DOIT Esp32 DevKit v1 (30 pins long, 11 pins width) by Werner Rothschopf (modified by vanepp Dec 2018)
