# Fritzing sketch practice09 (saved by Fritzing 0.9.5d)
breadboards: 1

parts:
  U1 = LuaNode32 / ESP32 [part_number=ESP32S-PIN30]
  R1 = Resistor [tolerance=±5% resistance=220 package="2010 [SMD]"]  # not connected
  LED1 = LED - 5mm [color="Red (633nm)" package="5 mm [THT]"]
  A2 = am312 pir sensor [package=THT]

nets:
  N1: U1.D13, LED1.anode
  N2: U1.GND, A2.pin3
  N3: U1.3V3, A2.pin1
  N4: U1.D4, A2.pin2

notes:
  +
  OUT
  -

custom parts:
  LuaNode32 / ESP32: New Image for LuaNode32 DOIT ESP32 DEVKIT V1. Base parts from LuaNode32 / ESP32 ESP32 based LuaNode32 by G.Noorlander DOIT Esp32 DevKit v1 (30 pins long, 11 pins width) by Werner Rothschopf (modified by vanepp Dec 2018)
  am312 pir sensor: The AM312 is an ultra-miniature PIR module which uses a pyroelectric sensor similar to the one found in the common SR501 but in a more compact form factor.
