# Fritzing sketch 2morter (saved by Fritzing 0.9.5d)
breadboards: 1

parts:
  U1 = LuaNode32 / ESP32 [part_number=ESP32S-PIN30]
  M3 = DC Motor
  L298N1 = L298N DC motor driver
  M4 = DC Motor
  U2 = LIPO-2000mAh [package=lipo-2000]

nets:
  GND: U1.GND, L298N1.GND
  VIN: U1.Vin, L298N1.5V
  N1: U1.D4, L298N1.ENB
  N2: U1.RX2, L298N1.IN4
  N3: U1.TX2, L298N1.IN3
  N4: U1.D18, L298N1.IN2
  N5: U1.D19, L298N1.IN1
  N6: U1.D21, L298N1.ENA
  N7: M3.pin_1, L298N1.OUT2
  N8: M3.pin_2, L298N1.OUT1
  N9: L298N1.OUT3, M4.pin_2
  N10: L298N1.OUT4, M4.pin_1
  N11: L298N1.12V, U2.+, U2.-

custom parts:
  LuaNode32 / ESP32: New Image for LuaNode32 DOIT ESP32 DEVKIT V1. Base parts from LuaNode32 / ESP32 ESP32 based LuaNode32 by G.Noorlander DOIT Esp32 DevKit v1 (30 pins long, 11 pins width) by Werner Rothschopf (modified by vanepp Dec 2018)
  L298N DC motor driver: 2x DC motor driver with 78M05 positive voltage regulator (7..35 V) L298N: max 46 V, 2 A Set 5 V Enable jumper to enable 5 V regultor (needed for the L298N) and +5 V output at screw terminal or supply external +5 V at screw terminal Set ENA and/or ENB to +5 V to enable motor permanently or supply ENA and/or ENB with PWM signal IN1 and IN2 set rotation directory for motor A (OUT1/OUT2) IN2 and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
